# Fritzing sketch Dimer2 (saved by Fritzing 0.8.5b)
circuit board: 8.46667cm x 5.64444cm
breadboards: 1

parts:
  U1 = attiny85 [package=dip]
  RE1 = Rotary Encoder [package=THT]
  S1 = Pushbutton [package="[THT]"]
  R1 = Resistor [package="2010 [SMD]"]
  R2 = Resistor [package="2010 [SMD]"]
  R3 = Resistor [package="2010 [SMD]"]
  VCC1 = 4 x AAA Battery Mount

nets:
  N1: U1.Pin_2, RE1.EncoderPinB, R3.Pin_0
  N2: U1.Pin_3, RE1.EncoderPinA, R2.Pin_0
  N3: U1.Pin_4, RE1.EncoderPinC, S1.Pin_3, S1.Pin_4, VCC1.-
  N4: U1.Pin_5, S1.Pin_1, S1.Pin_2, R1.Pin_1
  N5: U1.Pin_8, R1.Pin_0, R2.Pin_1, R3.Pin_1, VCC1.+
